# Fritzing sketch blimpCore (saved by Fritzing 0.6.5b)
breadboards: 1

parts:
  IC1 = L293D [package=THT]
  M1 = DC Motor
  M2 = DC Motor
  C1 = Electrolytic Capacitor [capacitance=10μF voltage=50V package="0605 [SMD, electrolytic]"]
  C3 = Ceramic Capacitor [capacitance=0.22µF voltage=5V package="0603 [SMD, multilayer]"]
  C2 = Ceramic Capacitor [capacitance=0.22µF voltage=5V package="0603 [SMD, multilayer]"]
  Arduino1 = Arduino
  VCC1 = Battery
  U2 = mystery part, 4 pins [chip_label=RX_1 spacing=300mil]
  U3 = mystery part, 4 pins [chip_label=RX_2 spacing=300mil]
  ANT1 = Antenna

nets:
  N1: IC1.Enable_1, Arduino1.D6
  N2: IC1.In_1, Arduino1.D5
  N3: IC1.Out_1_(_Controlled_by_Enable_1_), M2.pin_2, C3.0
  N4: IC1.0V, C1.-, Arduino1.GND, VCC1.-, U2.pin1, U3.pin2, U3.pin3
  N5: IC1.Out_2_(_Controlled_by_Enable_1_), M2.pin_1, C3.1
  N6: IC1.In_2, Arduino1.D4
  N7: IC1.+Vmotor, C1.+, VCC1.+
  N8: IC1.Enable_2, Arduino1.D9
  N9: IC1.In_3, Arduino1.D7
  N10: IC1.Out_3_(_Controlled_by_Enable_2_), M1.pin_2, C2.1
  N11: IC1.Out_4_(_Controlled_by_Enable_2_), M1.pin_1, C2.0
  N12: IC1.In_4, Arduino1.D8
  N13: IC1.+V, Arduino1.+5V, U2.pin4, U3.pin1
  N14: Arduino1.D0RX, U2.pin2
  N15: U3.pin4, ANT1.antenna_lead
