# Fritzing sketch blimpTx (saved by Fritzing 0.7.0b)
perfboards: 1

parts:
  Arduino1 = Arduino
  J2 = male pin header, 5 pins [form="♂ (male)"]
  J4 = male pin header, 5 pins [form="♂ (male)"]  # not connected
  J3 = male pin header, 4 pins [form="♂ (male)"]
  J1 = rounded female pin header, 5 pins [form="♀ (female rounded)"]
  D1 = Rectifier Diode [part_number=1N4001 package="300 mil [THT]"]

nets:
  N1: Arduino1.D3, J2.pin2, J1.pin4
  N2: Arduino1.+5V, J3.pin1, J1.pin3
  N3: Arduino1.GND, J3.pin2, D1.cathode
  N4: J1.pin5, D1.anode

notes:
  [1] ANT extension [2] ANT [3] Vss [4] D3 [5] GND
