# Fritzing sketch powerSupply (saved by Fritzing 0.7.0b)
stripboards: 1

parts:
  U1 = Voltage Regulator - 5V [package="DPak [SMD]"]
  D1 = Rectifier Diode [part_number=1N4001 package="Melf DO-213 AB [SMD]"]
  C1 = Electrolytic Capacitor [capacitance=1000µF package="300 mil [THT, electrolytic]"]
  J1 = male pin header, 2 pins [form="♂ (male)"]
  D2 = Rectifier Diode [part_number=1N4001 package="Melf DO-213 AB [SMD]"]
  J2 = male pin header, 2 pins [form="♂ (male)"]
  J3 = male pin header, 2 pins [form="♂ (male)"]
  J4 = rounded female pin header, 2 pins [form="♀ (female rounded)"]
  J5 = rounded female pin header, 2 pins [form="♀ (female rounded)"]
  C2 = Electrolytic Capacitor [capacitance=1000µF package="300 mil [THT, electrolytic]"]
  Part1 = Arduino Pro Mini 3.3V
  Part2 = FTDI Basic Programmer

nets:
  N1: U1.input_voltage, D1.cathode
  GND: U1.GND, C1.-, J1.pin1, J2.pin2, J3.pin2, J4.pin2, J5.pin2, C2.-, Part1.GND, Part2.CTS, Part2.GND
  N2: U1.output_voltage, D2.anode
  N3: D1.anode, J1.pin2, C2.+
  N4: C1.+, D2.cathode, J2.pin1, J3.pin1, J4.pin1, J5.pin1, Part1.RAW
  N5: Part1.DTR, Part2.DTR
  N6: Part1.TXO, Part2.RXI
  N7: Part1.RXI, Part2.TXO
  N8: Part1.VCC, Part2.POWER

notes:
  7.4V in
  regulated 5V out
