# Fritzing sketch strippedArduino (saved by Fritzing 0.7.0b)
stripboards: 1

parts:
  U1 = atmega168 [package="DIP28 [THT]"]
  C1 = Ceramic Capacitor [capacitance=22pF package="100 mil [THT, multilayer]"]
  XTAL1 = Crystal [frequency="16 Mhz" package=THT]
  C2 = Ceramic Capacitor [capacitance=22pF package="100 mil [THT, multilayer]"]
  U2 = Voltage Regulator - 5V [package="TO220 [THT]"]
  C3 = Electrolytic Capacitor [capacitance=1µF package="100 mil [THT, electrolytic]"]
  C4 = Electrolytic Capacitor [capacitance=1µF package="100 mil [THT, electrolytic]"]
  J2 = male pin header, 2 pins [form="♂ (male)"]
  D1 = Rectifier Diode [part_number=1N4001 package="300 mil [THT]"]
  C5 = Ceramic Capacitor [capacitance=0.47µF package="100 mil [THT, multilayer]"]
  R1 = Resistor [tolerance=±5% resistance=10k package=THT]
  J6 = male pin header, 6 pins [form="♂ (male)"]
  J5 = rounded female pin header, 5 pins [form="♀ (female rounded)"]
  J3 = rounded female pin header, 4 pins [form="♀ (female rounded)"]
  J4 = rounded female pin header, 8 pins [form="♀ (female rounded)"]
  J1 = rounded female pin header, 8 pins [form="♀ (female rounded)"]

nets:
  N1: U1.Pin_1, C5.0, J1.pin3
  N2: U1.Pin_2, J6.pin4, J1.pin4
  N3: U1.Pin_3, J6.pin5, J1.pin5
  N4: U1.Pin_4, J1.pin6
  N5: U1.Pin_5, J1.pin7
  N6: U1.Pin_6, J1.pin8
  N7: U1.Pin_7, U1.Pin_20, U2.output_voltage, C3.+, R1.Pin_0, J6.pin3, J4.pin1, J1.pin1
  N8: U1.Pin_8, U1.Pin_22, C1.0, C2.1, U2.GND, C3.-, C4.-, J2.pin1, J6.pin1, J4.pin2, J1.pin2
  N9: U1.Pin_9, C1.1, XTAL1.pin_0
  N10: U1.Pin_10, XTAL1.pin_1, C2.0
  N11: U1.Pin_11, J3.pin1
  N12: U1.Pin_12, J3.pin2
  N13: U1.Pin_13, J3.pin3
  N14: U1.Pin_14, J3.pin4
  N15: U1.Pin_15, J5.pin5
  N16: U1.Pin_16, J5.pin4
  N17: U1.Pin_17, J5.pin3
  N18: U1.Pin_18, J5.pin2
  N19: U1.Pin_19, J5.pin1
  N20: U1.Pin_23, J4.pin8
  N21: U1.Pin_24, J4.pin7
  N22: U1.Pin_25, J4.pin6
  N23: U1.Pin_26, J4.pin5
  N24: U1.Pin_27, J4.pin4
  N25: U1.Pin_28, J4.pin3
  N26: U2.input_voltage, C4.+, D1.cathode
  N27: J2.pin2, D1.anode
  N28: C5.1, R1.Pin_1, J6.pin6

notes:
  [1] Reset
  [2] D0 [Rx]
  [3] D1 [Tx]
  [4] D2
  [5] D3
  [6] D4
  [11] D5
  [12] D6
  [13] D7
  [14] D8
  [28] A5
  [27] A4
  [26] A3
  [25] A2
  [24] A1
  [23] A0
  [19] D13
  [18] D12
  [17] D11
  [16] D10
  [15] D9
