# Fritzing sketch blimp2 (saved by Fritzing 0.7.0b)
stripboards: 1

parts:
  IC1 = L293D [package=THT]
  C1 = Ceramic Capacitor [capacitance=0.22µF voltage=5V package="100 mil [THT, multilayer]"]
  C2 = Ceramic Capacitor [capacitance=0.22µF voltage=5V package="100 mil [THT, multilayer]"]
  J2 = male pin header, 2 pins [form="♂ (male)"]
  J4 = female pin header, 3 pins [form="♀ (female)"]
  J6 = male pin header, 2 pins [form="♂ (male)"]
  J7 = male pin header, 2 pins [form="♂ (male)"]
  J9 = female pin header, 4 pins [form="♀ (female)"]
  J10 = female pin header, 4 pins [form="♀ (female)"]
  J11 = female pin header, 2 pins [form="♀ (female)"]
  J12 = female pin header, 2 pins [form="♀ (female)"]
  J14 = female pin header, 2 pins [form="♀ (female)"]
  J13 = male pin header, 2 pins [form="♂ (male)"]
  J1 = male pin header, 3 pins [form="♂ (male)"]
  J5 = female pin header, 6 pins [form="♀ (female)"]
  C3 = Electrolytic Capacitor [capacitance=10µF voltage=50V package="100 mil [THT, electrolytic]"]
  D1 = Rectifier Diode [part_number=1N4004 package="300 mil [THT]"]
  D2 = Rectifier Diode [part_number=1N4004 package="300 mil [THT]"]
  C4 = Ceramic Capacitor [capacitance=0.22µF package="1206 [SMD, multilayer]"]

nets:
  N1: IC1.Enable_1, J4.pin2
  N2: IC1.In_1, J4.pin3
  N3: IC1.Out_1_(_Controlled_by_Enable_1_), C1.1, J7.pin1
  N4: IC1.0V, J2.pin2, J9.pin1, J10.pin2, J10.pin3, J14.pin1, J13.pin1, J1.pin1, J5.pin4, C3.-, D1.cathode, D1.anode, C4.1
  N5: IC1.Out_2_(_Controlled_by_Enable_1_), C1.0, J7.pin2
  N6: IC1.In_2, J4.pin1
  N7: IC1.+Vmotor, J2.pin1, C3.+
  N8: IC1.Enable_2, J5.pin3
  N9: IC1.In_3, J5.pin2
  N10: IC1.Out_3_(_Controlled_by_Enable_2_), C2.1, J6.pin2
  N11: IC1.Out_4_(_Controlled_by_Enable_2_), C2.0, J6.pin1
  N12: IC1.In_4, J5.pin1
  N13: IC1.+V, J9.pin4, J10.pin1, J1.pin2, J5.pin5, C4.0
  N14: J9.pin2, J12.pin1
  N15: J9.pin3, J12.pin2
  N16: J10.pin4, J11.pin1, J11.pin2
  N17: J14.pin2, J13.pin2, D2.cathode, D2.anode
  N18: J1.pin3, J5.pin6

notes:
  L293D
  [1] IN4
  [2] IN3
  [3] ENABLE2
  [4]GND
  [5]VSS
  [6] Servo (IN1)
  Servo Port
  [1] GND
  [2] VSS
  [3] IN1
  L293D
  [1] IN1
  [2] ENABLE1
  [3] IN2
  Rx
  ANT
  Rx
  [1] VCC
  [2] GND
  [3] GND
  [4] ANT
  Rx
  [1] GND
  [2] DOUT
  [3] LOUT
  [4] VCC
  Rx
  DOUT (Ard)
  Ard_Batt
  [1] GND
  [2] VIN
  Ard
  [1] GND(x)
  [2] VIN
