# Fritzing sketch blimp3 (saved by Fritzing 0.7.0b)
stripboards: 2

parts:
  IC1 = L293D [package=THT]
  Part1 = Logic Level Converter
  Part2 = Arduino Pro Mini 3.3V
  U2 = Voltage Regulator - 5V [package="TO220 [THT]"]
  U3 = Voltage Regulator - 3.3V [package="TO220 [THT]"]
  J1 = male pin header, 2 pins [form="♂ (male)"]
  D1 = Rectifier Diode [part_number=1N4001 package="300 mil [THT]"]
  C1 = Electrolytic Capacitor [capacitance=200µF package="1010 [SMD, electrolytic]"]
  C2 = Electrolytic Capacitor [capacitance=200µF package="1010 [SMD, electrolytic]"]
  S1 = Toggle Switch [package=THT]
  D2 = Rectifier Diode [part_number=1N4001 package="300 mil [THT]"]
  C3 = Ceramic Capacitor [capacitance=22µF package="1206 [SMD, multilayer]"]
  J2 = male pin header, 2 pins [form="♂ (male)"]
  J3 = male pin header, 2 pins [form="♂ (male)"]
  C4 = Ceramic Capacitor [capacitance=22µF package="1206 [SMD, multilayer]"]
  C5 = Ceramic Capacitor [capacitance=22µF package="1206 [SMD, multilayer]"]
  J4 = male pin header, 2 pins [form="♂ (male)"]
  D3 = Rectifier Diode [part_number=1N4001 package="300 mil [THT]"]
  S2 = Toggle Switch [package=THT]
  J5 = male pin header, 7 pins [form="♂ (male)"]
  J6 = male pin header, 7 pins [form="♂ (male)"]
  C7 = Ceramic Capacitor [capacitance=22µF package="1206 [SMD, multilayer]"]
  J7 = female pin header, 10 pins [form="♀ (female)"]  # not connected
  J8 = female pin header, 10 pins [form="♀ (female)"]
  C9 = Electrolytic Capacitor [capacitance=200µF package="1010 [SMD, electrolytic]"]
  C10 = Ceramic Capacitor [capacitance=22µF package="1206 [SMD, multilayer]"]
  C11 = Ceramic Capacitor [capacitance=22µF package="1206 [SMD, multilayer]"]
  C12 = Ceramic Capacitor [capacitance=22µF package="1206 [SMD, multilayer]"]
  S3 = Toggle Switch [package=THT]  # not connected
  S4 = Toggle Switch [package=THT]  # not connected
  C13 = Ceramic Capacitor [capacitance=22µF package="1206 [SMD, multilayer]"]
  Q1 = npn-Powertransistor [part_number=TIP102 package="TO220 [THT]"]
  J9 = male pin header, 2 pins [form="♂ (male)"]
  D4 = Rectifier Diode [part_number=1N4001 package="300 mil [THT]"]
  C14 = Ceramic Capacitor [capacitance=22µF package="1206 [SMD, multilayer]"]
  U4 = Voltage Regulator - 5V [package="TO220 [THT]"]

nets:
  N1: IC1.Enable_1, Part2.D5
  N2: IC1.In_1, Part2.D7
  N3: IC1.Out_1_(_Controlled_by_Enable_1_), J2.pin1, C5.0
  GND: IC1.0V, Part1.RX2_LV, Part1.GND, Part2.GND, U2.GND, U3.GND, J1.pin2, C1.-, C2.-, C3.0, J4.pin1, J5.pin1, J6.pin1, C7.1, J8.pin10, C9.-, C10.0, C11.1, C12.1, C13.0, Q1.emitter, U4.GND
  N4: IC1.Out_2_(_Controlled_by_Enable_1_), J2.pin2, C5.1
  N5: IC1.In_2, Part2.D6
  N6: IC1.+Vmotor, U4.input_voltage
  N7: IC1.Enable_2, Part2.D10
  N8: IC1.In_3, Part2.D8
  N9: IC1.Out_3_(_Controlled_by_Enable_2_), J3.pin2, C4.0
  N10: IC1.Out_4_(_Controlled_by_Enable_2_), J3.pin1, C4.1
  N11: IC1.In_4, Part2.D9
  N12: IC1.+V, Part1.HV, Part2.RAW, U3.input_voltage, D2.cathode, C3.1, J5.pin2, J6.pin2, C7.0, C11.0, C12.0
  N13: Part1.TX2_LV, J8.pin6
  N14: Part1.LV, U3.output_voltage, J8.pin1, C9.+, C10.1, C13.1
  N15: Part1.RX2_HV, Part2.TXO
  N16: Part1.TX2_HV, Part2.RXI
  N17: Part2.A4, Part2.A2
  N18: Part2.A5, Part2.A3
  N19: Part2.A1, J6.pin5
  N20: Part2.A0, J5.pin5
  N21: Part2.MOSI, Q1.base
  N22: U2.input_voltage, D1.cathode, C1.+
  N23: U2.output_voltage, C2.+, D2.anode
  N24: J1.pin1, S1.L1
  N25: J4.pin2, S2.L2, J9.pin1, D4.cathode, C14.1
  N26: D3.cathode, U4.output_voltage
  N27: D3.anode, S2.COM
  N28: J8.pin2, J8.pin5
  N29: J8.pin3, J8.pin9
  N30: Q1.collector, J9.pin2, D4.anode, C14.0

notes:
  Sonars
  Arduino
  3.7 V
  Steering Motors
  7.4 V IN
  5 V OUT
  3 V OUT
  Xbee
  Elevation Motor Relay
  Logic Converter
