# Fritzing sketch MOD_1_power-supply (saved by Fritzing 0.7.1b)
breadboards: 1

parts:
  U1 = Voltage Regulator - 5V [package="TO220 [THT]"]
  U2 = Voltage Regulator - 3.3V [package="TO220 [THT]"]
  J1 = male pin header, 2 pins [form="♂ (male)"]
  D1 = Rectifier Diode [part_number=1N4001 package="300 mil [THT]"]
  J3 = female pin header, 2 pins [form="♀ (female)"]
  C2 = Electrolytic Capacitor [capacitance=1µF package="100 mil [THT, electrolytic]"]
  C3 = Electrolytic Capacitor [capacitance=1µF package="100 mil [THT, electrolytic]"]
  C4 = Electrolytic Capacitor [capacitance=1µF package="100 mil [THT, electrolytic]"]
  J2 = female pin header, 2 pins [form="♀ (female)"]
  D2 = Rectifier Diode [part_number=1N4001 package="300 mil [THT]"]
  C5 = Electrolytic Capacitor [capacitance=1µF package="100 mil [THT, electrolytic]"]
  Part1 = Arduino Pro Mini 3.3V

nets:
  N1: U1.input_voltage, C3.+, D2.cathode
  GND: U1.GND, U2.input_voltage, J1.pin2, C2.-, C3.-, C4.-, C5.-, Part1.A4, Part1.GND
  N2: U1.output_voltage, U2.output_voltage, C4.+, Part1.RAW
  N3: U2.GND, J2.pin1, C5.+
  N4: J1.pin1, D1.anode
  N5: D1.cathode, C2.+, J2.pin2
  N6: J3.pin1, D2.anode
  N7: J3.pin2, Part1.VCC

notes:
  MOD 1 - power supply [DONE]
  3.7 V
  motor
  supply
  7.2V DC supply
  3.3V Vcc | MTR Vcc
  Ld1117V33 V-Reg
  7805 V-Reg
