# Fritzing sketch blimp3-tx (saved by Fritzing 0.7.1b)

parts:
  Part1 = Logic Level Converter
  J1 = female pin header, 10 pins [form="♀ (female)"]  # not connected
  J2 = female pin header, 10 pins [form="♀ (female)"]
  C1 = Ceramic Capacitor [capacitance=100nF package="100 mil [THT, multilayer]"]
  C2 = Ceramic Capacitor [capacitance=100nF package="100 mil [THT, multilayer]"]
  C3 = Ceramic Capacitor [capacitance=100nF package="100 mil [THT, multilayer]"]
  C4 = Electrolytic Capacitor [capacitance=1µF package="100 mil [THT, electrolytic]"]
  Arduino1 = Arduino
  S1 = Toggle Switch [package=THT]
  S2 = Toggle Switch [package=THT]

nets:
  N1: Part1.TX2_LV, S1.L1
  N2: Part1.RX2_LV, S2.L1
  GND: Part1.GND, J2.pin10, C1.1, C2.1, C3.1, C4.-, Arduino1.GND
  N3: Part1.LV, J2.pin1, C2.0, C3.0, C4.+, Arduino1.3V3
  N4: Part1.HV, C1.0, Arduino1.+5V
  N5: Part1.RX2_HV, Arduino1.D3
  N6: Part1.TX2_HV, Arduino1.D2
  N7: J2.pin2, S1.COM
  N8: J2.pin3, S2.COM
