# Fritzing sketch blimp4-schematic (saved by Fritzing 0.7.1b)
breadboards: 1

parts:
  Part1 = Arduino Pro Mini 3.3V
  DC_Power1 = DC Power [voltage=7.2]
  U1 = Voltage Regulator - 5V [package="DPak [SMD]"]
  U2 = Voltage Regulator - 3.3V [package="TO220 [THT]"]
  C1 = Ceramic Capacitor [capacitance=0.22µF package="0603 [SMD, multilayer]"]
  D1 = Rectifier Diode [part_number=1N4001 package="300 mil [THT]"]
  D2 = Rectifier Diode [part_number=1N4001 package="300 mil [THT]"]
  C2 = Electrolytic Capacitor [capacitance=200µF voltage=15.0V package="100 mil [THT, electrolytic]"]
  S1 = Toggle Switch [package=THT]
  C3 = Electrolytic Capacitor [capacitance=200µF voltage=15.0V package="100 mil [THT, electrolytic]"]
  IC1 = L293D [package=THT]
  C4 = Ceramic Capacitor [capacitance=0.22µF package="0603 [SMD, multilayer]"]
  M1 = DC Motor
  M2 = DC Motor
  DC_Power2 = DC Power [voltage=5]
  D3 = Rectifier Diode [part_number=1N4001 package="300 mil [THT]"]
  C5 = Electrolytic Capacitor [capacitance=200µF voltage=15.0V package="100 mil [THT, electrolytic]"]
  C6 = Ceramic Capacitor [capacitance=0.22µF package="0603 [SMD, multilayer]"]
  S2 = Toggle Switch [package=THT]
  Part2 = Logic Level Converter
  C7 = Electrolytic Capacitor [capacitance=200µF voltage=15.0V package="100 mil [THT, electrolytic]"]
  C8 = Ceramic Capacitor [capacitance=0.22µF package="0603 [SMD, multilayer]"]
  C9 = Ceramic Capacitor [capacitance=0.22µF package="0603 [SMD, multilayer]"]
  U3 = XBee
  S3 = Toggle Switch [package=THT]
  S4 = Toggle Switch [package=THT]
  C10 = Ceramic Capacitor [capacitance=0.22µF package="0603 [SMD, multilayer]"]
  U5 = mystery part, 7 pins [chip_label=Sonar spacing=300mil]
  U6 = mystery part, 7 pins [chip_label=Sonar spacing=300mil]
  C11 = Ceramic Capacitor [capacitance=0.22µF package="0603 [SMD, multilayer]"]
  C12 = Ceramic Capacitor [capacitance=0.22µF package="0603 [SMD, multilayer]"]
  Q1 = NPN-Transistor [package="TO92 [THT]"]
  M3 = DC Motor
  U8 = mystery part, 2 pins [chip_label=CMOS spacing=300mil]
  C13 = Ceramic Capacitor [capacitance=0.22µF package="0603 [SMD, multilayer]"]
  D5 = Rectifier Diode [part_number=1N4001 package="300 mil [THT]"]
  D4 = Rectifier Diode [part_number=1N4001 package="300 mil [THT]"]

nets:
  GND: Part1.GND, U1.GND, U2.GND, C1.1, S1.L1, C3.-, IC1.0V, C4.1, DC_Power2.GND, C5.-, C6.1, Part2.GND, C7.-, C8.1, C9.0, U3.GND, C10.1, U5.pin1, U6.pin1, C11.1, C12.1, M3.pin_2, C13.0, D4.cathode
  N1: Part1.RAW, U1.output_voltage, C1.0, C3.+, IC1.+V, C4.0, Part2.HV, C9.1, U5.pin2, U6.pin2, C11.0, C12.0
  N2: Part1.A1, U5.pin5
  N3: Part1.A0, U6.pin5
  N4: Part1.MISO, Q1.B
  N5: Part1.D10, IC1.Enable_2
  N6: Part1.D9, IC1.In_4
  N7: Part1.D8, IC1.In_3
  N8: Part1.D7, IC1.In_1
  N9: Part1.D6, IC1.In_2
  N10: Part1.D5, IC1.Enable_1
  N11: Part1.RXI, Part2.TX_HV
  N12: Part1.TXO, Part2.RX_HV
  N13: DC_Power1.V+, D1.anode, D2.anode, C2.+, D5.anode
  N14: DC_Power1.GND, C2.-, S1.COM, U8.pin1
  N15: U1.input_voltage, D1.cathode
  N16: U2.input_voltage, D2.cathode
  N17: U2.output_voltage, Part2.LV, C7.+, C8.0, U3.VCC, C10.0
  N18: IC1.Out_1_(_Controlled_by_Enable_1_), M1.pin_2
  N19: IC1.Out_2_(_Controlled_by_Enable_1_), M1.pin_1
  N20: IC1.+Vmotor, D3.cathode, C6.0, Q1.C
  N21: IC1.Out_3_(_Controlled_by_Enable_2_), M2.pin_2
  N22: IC1.Out_4_(_Controlled_by_Enable_2_), M2.pin_1
  N23: DC_Power2.V+, C5.+, S2.COM
  N24: D3.anode, S2.L2
  N25: Part2.RX_LV, S3.COM
  N26: Part2.TX_LV, S4.COM
  N27: U3.pin2, S4.L2
  N28: U3.pin3, S3.L2
  N29: Q1.E, M3.pin_1, D4.anode
  N30: U8.pin2, C13.1, D5.cathode

notes:
  mod 6
  mod 5
  mod 4
  mod 3
  mod 2
  mod 1
